# Fritzing sketch ClockDS1302_4DigitsDisplay (saved by Fritzing 0.9.3b)
breadboards: 1

parts:
  Componente1 = Arduino Uno (Rev3)
  IC1 = DS1302 [package="SO8 [SMD]"]  # not connected
  Y1 = CRYSTAL [package=crystal-32khz-smd_epson_mc146]  # not connected
  LED2 = 7-SEGMENT-4DIGIT-YOUNGSUN [package=7-segment-4digit-youngsun-longpads]

nets:
  N1: Componente1.D8, LED2.DP
  N2: Componente1.D1/TX, LED2.A
  N3: Componente1.D2, LED2.B
  N4: Componente1.D3_PWM, LED2.C
  N5: Componente1.D4, LED2.D
  N6: Componente1.D5_PWM, LED2.E
  N7: Componente1.D6_PWM, LED2.F
  N8: Componente1.D7, LED2.G
