# Fritzing sketch EthernetShield_DTH11 (saved by Fritzing 0.9.3b)

parts:
  Componente1 = Arduino Uno (Rev3)  # not connected
  Componente2 = Arduino Ethernet Shield (Rev3)
  Part2 = KY-015 Temperature & Humidity Sensor Module [package="Breakout board"]

nets:
  N1: Componente2.A0, Part2.Vin
  N2: Componente2.5V, Part2.S
  N3: Componente2.GND, Part2.-

custom parts:
  KY-015 Temperature & Humidity Sensor Module: KY-015 temperature and humidity sensor module, provides a low-latency serial interface to measure humidity and temperature.
