# Fritzing sketch Soil_Moisture_Sensor (saved by Fritzing 0.9.3b)

parts:
  Componente1 = Soil Moisture Sensor
  Componente2 = Arduino Uno (Rev3)

nets:
  N1: Componente1.SIG, Componente2.A0
  GND: Componente1.GND, Componente2.GND
  VCC: Componente1.VCC, Componente2.5V
